# Fritzing sketch moter_1 (saved by Fritzing 0.9.3b)
breadboards: 1

parts:
  U1 = L9110 H-bridge module [part_number="L9110 H-bridge"]
  パーツ2 = Arduino Nano (Rev3.0)
  VCC1 = Battery
  M1 = Stepper Motor - Unipolar
  U3 = Thumb Joystick [package=joystick]

nets:
  N1: U1.MOTOR_A-A, M1.D
  N2: U1.MOTOR_A-B, M1.A
  N3: パーツ2.GND, VCC1.-, M1.COMMON_1, U3.SEL+
  N4: パーツ2.D4, M1.C
  N5: パーツ2.D5, M1.B
  N6: パーツ2.5V, U3.H+, U3.SEL-
  N7: パーツ2.A0, U3.V+
  N8: パーツ2.3V3, M1.COMMON_2

notes:
  ジョイコン
  左から
  ・GND
  ・A０
  ・5V
  ・GND
  ・A1
  ・５V
  モータ
  左から
  ・ドライバ(MOTER A)
  ・GND
  ・arudino(D4)
  ・arudino(D5)
  ・arudino(3V3)
  ・ドライバ(MOTER A)
  電源ボックス
  上から
  ・ドライバ(Vcc)
  ・GND
  ドライバ
  Moter A　左から
  ・モータ（一番左）
  ・モータ（一番右）
  下の段　左から
  ・GND
  ・電源(＋)
  ・arudino(D3)
  ・arudino(D2)
  arudino（試作段階ではnano every を使用）
  ・D2→ドライバ(A-1B)
  ・D3→ドライバ(A-1A)
  ・D4→モータ(feedback)
  ・D5→モータ(feedback)
  ・５V→ジョイコン(２本）
  ・3.3V→ジョイコン
  ・A0→ジョイコン
  ・A１→ジョイコン
